// Logisim project Atividade 01.circ as structural Verilog: 5 circuits, main circuit main
module main (
  input  in_1,
  input  in_2,
  input  in_3,
  input  in_4,
  input  in_5,
  input  in_6,
  input  in_7,
  output out_8,
  output out_9,
  output out_10,
  output out_11
);

  decod_hamming decod_hamming_1 (
    .p0(in_1), .p1(in_2), .d0(in_3), .p2(in_4), .d1(in_5), .d2(in_6), .d3(in_7), .d0_2(out_8), .d1_2(out_9),
    .d2_2(out_10), .d3_2(out_11));
endmodule

module gerador_paridade (
  input  d0,
  input  d1,
  input  d2,
  output p
);

  wire xor_1_out;

  xor xor_1 (xor_1_out, d0, d1);
  xor xor_2 (p, xor_1_out, d2);
endmodule

module comparador_paridades (
  input  p0,
  input  p1,
  input  p2,
  input  p0_prime,
  input  p1_prime,
  input  p2_prime,
  output e0,
  output e1,
  output e2
);

  xor xor_1 (e0, p0, p0_prime);
  xor xor_2 (e1, p1, p1_prime);
  xor xor_3 (e2, p2, p2_prime);
endmodule

module decod_hamming (
  input  p0,
  input  p1,
  input  d0,
  input  p2,
  input  d1,
  input  d2,
  input  d3,
  output d0_2,
  output d1_2,
  output d2_2,
  output d3_2
);

  wire comparador_paridades_1_e0, comparador_paridades_1_e1, comparador_paridades_1_e2, gerador_paridade_1_p,
       gerador_paridade_2_p, gerador_paridade_3_p;

  gerador_paridade gerador_paridade_1 (.d0(d0), .d1(d1), .d2(d3), .p(gerador_paridade_1_p));
  gerador_paridade gerador_paridade_2 (.d0(d0), .d1(d2), .d2(d3), .p(gerador_paridade_2_p));
  gerador_paridade gerador_paridade_3 (.d0(d1), .d1(d2), .d2(d3), .p(gerador_paridade_3_p));
  comparador_paridades comparador_paridades_1 (
    .p0(p0), .p1(p1), .p2(p2), .p0_prime(gerador_paridade_1_p), .p1_prime(gerador_paridade_2_p),
    .p2_prime(gerador_paridade_3_p), .e0(comparador_paridades_1_e0), .e1(comparador_paridades_1_e1),
    .e2(comparador_paridades_1_e2));
  corretor_erros corretor_erros_1 (.e0(d0_2), .e1(d1_2), .e2(d2_2), .d0(d3_2));  // open: d1, d2, d3
endmodule

module corretor_erros (
  input  e0,
  input  e1,
  input  e2,
  input  d0,
  input  d1,
  input  d2,
  input  d3
);

  wire and_1_out, and_2_out, and_3_out;

  and and_1 (and_1_out, e0, e1, ~e2);  // AND_Gate
  and and_2 (and_2_out, e0, ~e1, e2);  // AND_Gate
  and and_3 (and_3_out, ~e0, e1, e2);  // AND_Gate
endmodule
